# Fritzing sketch GreenhouseSensors (saved by Fritzing 0.9.2b)
breadboards: 1

parts:
  U1 = mystery part, 4 pins [chip_label=AM2315]
  J1 = screw terminal, 4 pins
  U2 = mystery part, 4 pins [chip_label=AM2315]
  J3 = screw terminal, 4 pins
  R2 = Resistor [tolerance=±5% resistance=10k package=THT]
  R3 = Resistor [tolerance=±5% resistance=10k package=THT]
  R4 = Resistor [tolerance=±5% resistance=10k package=THT]
  R5 = Resistor [tolerance=±5% resistance=10k package=THT]
  J4 = screw terminal, 3 pins
  U4 = mystery part, 3 pins [chip_label=Anemometer]
  J5 = Screw terminal - 2 pins [package=THT]
  Teensy_3_1 = Teensy 3.1
  U5 = mystery part, 6 pins [chip_label="Sparkfun MPL3115"]

nets (from the breadboard view):
  N1: U1.pin1, J1.pin4, R3.Pin_0
  N2: U1.pin2, J1.pin3, R4.Pin_0
  N3: U1.pin3, J1.pin2, U2.pin3, J3.pin2, R2.Pin_1, R3.Pin_1, R4.Pin_1, R5.Pin_1, Teensy_3_1.3V3, U5.pin5
  N4: U1.pin4, J1.pin1, U2.pin4, J3.pin1, J4.pin1, U4.pin3, J5.pin1, Teensy_3_1.GND, U5.pin6
  N5: U2.pin1, J3.pin4, R2.Pin_0, Teensy_3_1.A4/D18, U5.pin3
  N6: U2.pin2, J3.pin3, R5.Pin_0, Teensy_3_1.A5/D19, U5.pin4
  N7: J4.pin2, U4.pin2, J5.pin2

notes:
  9v supply
  Yellow=SCL1, Pin 29 Blue=SDA1, Pin 30
  These pins are on bottom of Teensy.
